# Fritzing sketch trinket_midi_to_midi (saved by Fritzing 0.9.4)
circuit board: 1.83173cm x 2.50185cm

parts:
  Part1 = Adafruit Trinket M0 [part_number="Adafruit #3500"]
  R1 = Resistor [tolerance=±5% resistance=1k package=THT]
  R2 = Resistor [tolerance=±5% resistance=1k package=THT]
  Part2 = Adafruit Trinket M0 [part_number="Adafruit #3500"]

nets:
  GND: Part1.GND, Part2.GND
  N1: Part1.D4_A2_PA06_TXD_MOSI, R2.Pin_1
  N2: Part1.D3_A3_PA07_RXD_SCK, R1.Pin_1
  N3: R1.Pin_0, Part2.D4_A2_PA06_TXD_MOSI
  N4: R2.Pin_0, Part2.D3_A3_PA07_RXD_SCK
